// Digital circuit 8 BIT ADDER.dig as structural Verilog
module _8_BIT_ADDER (
  input  [7:0] A,
  input  [7:0] B,
  input  CARRY_IN,
  output [7:0] SUM,
  output CARRY_OUT
);

  wire adder_1_carry, adder_2_carry, adder_3_carry, adder_4_carry, adder_5_carry, adder_6_carry,
       adder_7_carry;

  adder adder_1 (.A(A[0]), .B(B[0]), .C_in(CARRY_IN), .SUM(SUM[0]), .CARRY(adder_1_carry));
  adder adder_2 (.A(A[1]), .B(B[1]), .C_in(adder_1_carry), .SUM(SUM[1]), .CARRY(adder_2_carry));
  adder adder_3 (.A(A[2]), .B(B[2]), .C_in(adder_2_carry), .SUM(SUM[2]), .CARRY(adder_3_carry));
  adder adder_4 (.A(A[3]), .B(B[3]), .C_in(adder_3_carry), .SUM(SUM[3]), .CARRY(adder_4_carry));
  adder adder_5 (.A(A[4]), .B(B[4]), .C_in(adder_4_carry), .SUM(SUM[4]), .CARRY(adder_5_carry));
  adder adder_6 (.A(A[5]), .B(B[5]), .C_in(adder_5_carry), .SUM(SUM[5]), .CARRY(adder_6_carry));
  adder adder_7 (.A(A[6]), .B(B[6]), .C_in(adder_6_carry), .SUM(SUM[6]), .CARRY(adder_7_carry));
  adder adder_8 (.A(A[7]), .B(B[7]), .C_in(adder_7_carry), .SUM(SUM[7]), .CARRY(CARRY_OUT));
endmodule
