// Digital circuit ALU.dig as structural Verilog
module ALU (
  input  [7:0] A,
  input  [7:0] B,
  input  A2,
  input  A1,
  input  A0,
  input  A3,
  output [7:0] OUTPUT
);

  wire [7:0] full_addsub_1_out, logic_block_1_out, multiplexer_1_out, shiftfun_1_leftout, shiftfun_1_rightout;

  FULL_ADDSUB full_addsub_1 (.B(B), .A(A), .MODE(A1), .OUT(full_addsub_1_out));
  LOGIC_BLOCK logic_block_1 (.A(A), .B(B), .MODE_SELECTION({A2, A1, A0}), .OUT(logic_block_1_out));
  SHIFTFUN shiftfun_1 (
    .A(A), .B(B), .SELECTION(A1), .SHIFT_SELECTION(A0), .LEFTOUT(shiftfun_1_leftout),
    .RIGHTOUT(shiftfun_1_rightout));
  Multiplexer #(.Bits(8)) multiplexer_1 (
    .sel(A0), .in_0(shiftfun_1_leftout), .in_1(shiftfun_1_rightout), .out(multiplexer_1_out));
  Multiplexer #(.Selector_Bits(2), .Bits(8)) multiplexer_2 (
    .sel({A3, A2}), .in_0(logic_block_1_out), .in_1(logic_block_1_out), .in_2(full_addsub_1_out),
    .in_3(multiplexer_1_out), .out(OUTPUT));
endmodule
