// Digital circuit FULL ADDSUB.dig as structural Verilog
module FULL_ADDSUB (
  input  [7:0] B,
  input  [7:0] A,
  input  MODE,
  output [7:0] OUT
);

  wire [7:0] xor_1_out;
  wire [8:0] multiplexer_1_out;

  Multiplexer #(.Bits(9)) multiplexer_1 (.sel(MODE), .in_0({9{1'b0}}), .in_1({9{1'b1}}), .out(multiplexer_1_out));
  assign xor_1_out = B ^ multiplexer_1_out[8:1];  // XOr xor_1, 8 bits wide
  _8_BIT_ADDER _8_bit_adder_1 (.A(A), .B(xor_1_out), .CARRY_IN(multiplexer_1_out[0]), .SUM(OUT));  // open: CARRY_OUT
endmodule
