// Digital circuit adder.dig as structural Verilog
module adder (
  input  A,
  input  B,
  input  C_in,
  output SUM,
  output CARRY
);

  wire and_1_out, and_2_out, xor_1_out;

  and and_1 (and_1_out, A, B);
  xor xor_1 (xor_1_out, A, B);
  xor xor_2 (SUM, xor_1_out, C_in);
  and and_2 (and_2_out, xor_1_out, C_in);
  or or_1 (CARRY, and_1_out, and_2_out);
endmodule
