// Digital circuit LOGIC BLOCK.dig as structural Verilog
module LOGIC_BLOCK (
  input  [7:0] A,
  input  [7:0] B,
  input  [2:0] MODE_SELECTION,
  output [7:0] OUT
);

  wire [7:0] and_1_out, multiplexer_1_out, or_1_out, xor_1_out;

  assign and_1_out = A & B;  // And and_1, 8 bits wide
  assign or_1_out = A | B;  // Or or_1, 8 bits wide
  assign xor_1_out = A ^ B;  // XOr xor_1, 8 bits wide
  Multiplexer #(.Bits(8), .Selector_Bits(2)) multiplexer_1 (
    .sel(MODE_SELECTION[1:0]), .in_0(and_1_out), .in_1(or_1_out), .in_2(xor_1_out), .in_3(A),
    .out(multiplexer_1_out));
  assign OUT = multiplexer_1_out ^ {8{MODE_SELECTION[2]}};  // XOr xor_2, 8 bits wide
endmodule
