// Digital circuit SHIFTFUN.dig as structural Verilog
module SHIFTFUN (
  input  [7:0] A,
  input  [7:0] B,
  input  SELECTION,
  input  SHIFT_SELECTION,
  output [7:0] LEFTOUT,
  output [7:0] RIGHTOUT
);

  wire [0:0] demultiplexer_1_out_1;
  wire [7:0] multiplexer_1_out;
  wire [7:7] demultiplexer_1_out_0;

  Multiplexer #(.Bits(8)) multiplexer_1 (.sel(SELECTION), .in_0(A), .in_1(B), .out(multiplexer_1_out));
  Demultiplexer #(.Bits(8)) demultiplexer_1 (
    .sel(SHIFT_SELECTION), .in(multiplexer_1_out), .out_0({demultiplexer_1_out_0[7], LEFTOUT[7:1]}),
    .out_1({RIGHTOUT[6:0], demultiplexer_1_out_1[0]}));

  assign LEFTOUT[0] = 1'b0;
  assign RIGHTOUT[7] = 1'b0;
endmodule
